# Fritzing sketch TowerStack (saved by Fritzing 0.8.7b)
breadboards: 1

parts:
  Arduino = Arduino Uno (Rev3)
  8x8_LED_Display = 1.2 Inch 8x8 LED Matrix Backpack
  Wireless_Tranceiver_Module = nRF24L01 [package=module]
  Switch = SPST Switch [package=switch-spdt_kit]
  6V_(Four_AA_batteries) = 4 x AAA Battery Mount
  Button = SWITCH-MOMENTARY-2 [package=tactile-switch-1101ne]
  Resistor = Resistor [tolerance=±5% resistance=220 package=THT]
  Motor_Shield = Adafruit Motor/Stepper/Servo Shield
  DC_Motor = DC Motor
  Wireless_Tranceiver_Module_2 = nRF24L01 [package=module]
  Switch_2 = SPST Switch [package=switch-spdt_kit]
  6V_(Four_AA_batteries)_2 = 4 x AAA Battery Mount

nets:
  N1: Arduino.D8, Wireless_Tranceiver_Module.CSN
  N2: Arduino.D11_PWM/MOSI, Wireless_Tranceiver_Module.MOSI
  N3: Arduino.D12/MISO, Wireless_Tranceiver_Module.MISO
  N4: Arduino.D13/SCK, Wireless_Tranceiver_Module.SCK
  GND: Arduino.GND, 8x8_LED_Display.GND, Wireless_Tranceiver_Module.GND, Switch.S, 6V_(Four_AA_batteries).+, Resistor.Pin_1
  N5: Arduino.A4/SDA, 8x8_LED_Display.SDA
  N6: Arduino.A5/SCL, 8x8_LED_Display.SCL
  N7: Arduino.D2, Button.2, Resistor.Pin_0
  N8: Arduino.D7, Wireless_Tranceiver_Module.CE
  3V3: Arduino.3V3, Wireless_Tranceiver_Module.VCC
  5V: Arduino.5V, 8x8_LED_Display.VDD, Switch.P, Button.1
  N9: Switch.O, 6V_(Four_AA_batteries).-
  N10: Motor_Shield.D6, Wireless_Tranceiver_Module_2.CE
  N11: Motor_Shield.D7, Wireless_Tranceiver_Module_2.CSN
  GND_2: Motor_Shield.GND, Wireless_Tranceiver_Module_2.GND, Switch_2.S, 6V_(Four_AA_batteries)_2.+
  N12: Motor_Shield.M1B, DC_Motor.pin_1
  N13: Motor_Shield.M1A, DC_Motor.pin_2
  +3V3: Motor_Shield.+3V3, Wireless_Tranceiver_Module_2.VCC
  N14: Motor_Shield.D13, Wireless_Tranceiver_Module_2.SCK
  N15: Motor_Shield.D12, Wireless_Tranceiver_Module_2.MISO
  N16: Motor_Shield.D11, Wireless_Tranceiver_Module_2.MOSI
  N17: Motor_Shield.VMOTOR, Switch_2.P
  N18: Switch_2.O, 6V_(Four_AA_batteries)_2.-

custom parts:
  1.2 Inch 8x8 LED Matrix Backpack: This 1.2" 8x8 monochrome LED matrix includes a driver chip for simple control via an I2C interface. The backpack features address-selection jumpers so you can connect up to eight matrices on a single I2C bus.
  nRF24L01: nRF24L01 module
  Adafruit Motor/Stepper/Servo Shield: The original Adafruit Motorshield kit is one of our most beloved kits, which is why we decided to make something even better. We have upgraded the shield kit to make the bestest, easiest way to drive DC and Stepper motors. This shield will make quick work of your next robotics project! We kept the ability to drive up to 4 DC motors or 2 stepper motors, but added many improvements: Instead of a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
